# Fritzing sketch Net_Radio_schematic (saved by Fritzing 0.9.3b)

parts:
  MH-ET_Live_Minikit_for_ESP1 = MH-ET Live Minikit for ESP32
  SP1 = SPEAKER [package=pcb_mount_speaker]
  Componente1 = Adafruit MAX98357A I2S 3W Class D Amplifier [part_number="Adafruit #3006"]
  U1 = ENCODER-QUADRATURE [package=encoder-16mm-quad]
  S1 = Toggle Switch [package=THT]
  VCC1 = Battery

nets:
  GND: MH-ET_Live_Minikit_for_ESP1.GND, Componente1.GND, U1.B, VCC1.-
  N1: MH-ET_Live_Minikit_for_ESP1.IO26, Componente1.BCLK
  3.3V: MH-ET_Live_Minikit_for_ESP1.3.3V, Componente1.VIN
  N2: MH-ET_Live_Minikit_for_ESP1.IO22, Componente1.DIN
  N3: MH-ET_Live_Minikit_for_ESP1.IO16, U1.C
  N4: MH-ET_Live_Minikit_for_ESP1.VCC, S1.COM
  N5: MH-ET_Live_Minikit_for_ESP1.IO27, Componente1.LRCLK
  N6: MH-ET_Live_Minikit_for_ESP1.IO25, Componente1.GAIN
  N7: MH-ET_Live_Minikit_for_ESP1.IO4, U1.A
  N8: SP1.+, Componente1.VO-
  N9: SP1.-, Componente1.VO+
  N10: S1.L1, VCC1.+

custom parts:
  MH-ET Live Minikit for ESP32: MH-ET Live Minikit for ESP32 ( http://mh.nodebb.com/topic/8/mh-et-live-minikit-for-esp32/2/) PCB footprint is invalid.
  Adafruit MAX98357A I2S 3W Class D Amplifier: Listen to this good news - we now have an all in one digital audio amp breakout board that works incredibly well with the Raspberry Pi! If you're looking for an easy and low cost way to get you digital sound files bumpin' then the MAX08357 I2S Amp Breakout is for you. It takes standard I2S digital audio input and, not only decodes it into analog, but also amplifies it directly into a speaker.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
